# Fritzing sketch Thermostate_Sketch (saved by Fritzing 0.9.4)
breadboards: 2

parts:
  Part1 = Arduino Uno (Rev3) - ICSP
  LCD1 = LCD screen  # not connected
  R1 = Trimmer Potentiometer [maximum_resistance=10kΩ package=THT]
  R2 = Temperature Sensor (Thermistor) [thermistor_type=NTC package=THT]
  S1 = Pushbutton [package="[THT]"]
  R3 = Resistor [package="2010 [SMD]"]  # not connected
  R4 = Resistor [package="2010 [SMD]"]

nets:
  N1: Part1.A0, R2.pin_0, R4.Pin_0
  N2: Part1.5V, R1.leg1, R2.pin_1, S1.Pin_1, S1.Pin_2
  N3: Part1.D13/SCK, S1.Pin_3, S1.Pin_4
  N4: Part1.GND, R1.leg2

custom parts:
  Resistor: Resistor Basic schematic elements and footprints for 0603, 1206, and PTH resistors.
